# Fritzing sketch fritzing (saved by Fritzing 0.9.3b)
breadboards: 2

parts:
  KY-1 = Keyes Relay [package=THT]
  Part1 = RFID-RC522 [part_number=101218]
  Mod1 = KY-015 Temperature & Humidity Sensor Module [package="Breakout board"]
  J2 = Buzzer
  U2 = LuaNode32 / ESP32
  Part2 = LCD1602-I2C
  L2 = Solenoid
  Power_plug2 = Power plug

nets:
  N1: KY-1.signal, U2.D27
  VIN: KY-1.power, Mod1.Vin, U2.Vin, Part2.VCC
  GND: KY-1.ground, Part1.GND, Mod1.-, J2.pin1, U2.GND, Part2.GND
  N2: KY-1.C, Power_plug2.VCC
  N3: KY-1.NO, L2.pin2
  N4: Part1.SDA, U2.D5
  N5: Part1.SCK, U2.D18
  N6: Part1.MOSI, U2.D23
  N7: Part1.MISO, U2.D19
  N8: Part1.RST, U2.D4
  3.3V: Part1.3.3V, U2.3V3
  N9: Mod1.S, U2.D33
  N10: J2.pin2, U2.D32
  N11: U2.D21, Part2.SDA
  N12: U2.D22, Part2.SCL
  N13: L2.pin1, Power_plug2.GND

custom parts:
  Keyes Relay: The Keyes 5V relay module is suitable for SCM development, home appliance control. It uses a 5V~12V TIL control signal which can control DC / AC signal.
  KY-015 Temperature & Humidity Sensor Module: KY-015 temperature and humidity sensor module, provides a low-latency serial interface to measure humidity and temperature.
  Buzzer: Fixed frequency buzzer
  LuaNode32 / ESP32: ESP32 based LuaNode32
  LCD1602-I2C: A standard character display, usually with 2x16 characters. Comes in many colors with LCM1602 IIC attached.
